# Fritzing sketch Untitled Sketch 2 (saved by Fritzing 0.9.3b)
breadboards: 1

parts:
  Q2 = NPN-Transistor [package="TO92 [THT]"]
  R1 = Resistor [tolerance=±5% resistance=220 package=THT]
  LED1 = LED - 5mm [color="Red (633nm)" package="5 mm [THT]"]
  S1 = Pushbutton [package="[SMD]"]
  S2 = Pushbutton [package="[SMD]"]

nets:
  N1: Q2.E, S1.Pin_3, S1.Pin_4, S2.Pin_3, S2.Pin_4
  N2: Q2.B, S1.Pin_1, S1.Pin_2, S2.Pin_1, S2.Pin_2
  N3: R1.Pin_0, LED1.cathode
